# Fritzing sketch Perfboard (saved by Fritzing 0.9.4)
perfboards: 3

parts:
  Part1 = Arduino Nano (Rev3.0) (ICSP)
  J1 = Camdenboss CTB0158-2 [part_number=CTB0158-2 package=THT]  # not connected
  J3 = Camdenboss CTB0158-2 [part_number=CTB0158-2 package=THT]
  J4 = Camdenboss CTB0158-3 [part_number=CTB0158-3 package=THT]
  J2 = Camdenboss CTB0158-3 [part_number=CTB0158-3 package=THT]
  J5 = Camdenboss CTB0158-3 [part_number=CTB0158-3 package=THT]
  J6 = Camdenboss CTB0158-3 [part_number=CTB0158-3 package=THT]
  C1 = Capacitor Polarized [package=cpol-radial-100uf-25v]
  R2 = Resistor [tolerance=±5% resistance=220 package="1206 [SMD]"]
  R3 = Resistor [tolerance=±5% resistance=220 package="1206 [SMD]"]
  R5 = Resistor [tolerance=±5% resistance=220 package="1206 [SMD]"]
  R6 = Resistor [tolerance=±5% resistance=220 package="1206 [SMD]"]
  R8 = Resistor [tolerance=±5% resistance=220 package="1206 [SMD]"]
  U1 = 7-SEGMENT-DISPLAY [package=7-segment-display]
  R7 = Resistor [tolerance=±5% resistance=220 package="1206 [SMD]"]
  R10 = Resistor [tolerance=±5% resistance=220 package="1206 [SMD]"]  # not connected
  J7 = Camdenboss CTB0158-4 [part_number=CTB0158-4 package=THT]
  R11 = Resistor [tolerance=±5% resistance=220 package="1206 [SMD]"]  # not connected
  Q2 = Basic FET N-Channel [package="D2Pak [SMD]"]
  J8 = Camdenboss CTB0158-3 [part_number=CTB0158-3 package=THT]
  R12 = Resistor [tolerance=±5% resistance=220 package="1206 [SMD]"]
  J9 = Camdenboss CTB0158-2 [part_number=CTB0158-2 package=THT]  # not connected

nets:
  N1: Part1.D2, J7.pin3
  N2: Part1.D3, J7.pin2
  N3: Part1.D5, R12.Pin_0
  N4: Part1.D6, R8.Pin_0
  N5: Part1.D7, R7.Pin_0
  N6: Part1.D8, R2.Pin_0
  N7: Part1.D9, R3.Pin_0
  N8: Part1.D11/MOSI, R5.Pin_0
  N9: Part1.D12/MISO, R6.Pin_0
  N10: Part1.A7, J7.pin1
  N11: Part1.A4, J4.pin2
  N12: Part1.A3, J5.pin2
  N13: Part1.A2, J8.pin2
  N14: Part1.A1, J2.pin2
  N15: J3.pin1, J2.pin3
  N16: J3.pin2, Q2.Gate
  N17: J4.pin3, J5.pin3, J6.terminal_3
  N18: J2.pin1, J5.pin1, C1.-
  N19: R2.Pin_1, U1.E
  N20: R3.Pin_1, U1.G
  N21: R5.Pin_1, U1.G2
  N22: R6.Pin_1, U1.A
  N23: Q2.drain, R12.Pin_1

notes:
  TU-DO Dimmer Rev 1.1
  Notes:
  - Use female headers for the Arduino, 7-Seg disp and MOSFETs
